# Fritzing sketch BSProp (saved by Fritzing 0.9.0b)
breadboards: 2

parts:
  SPKR1 = Loudspeaker
  R7 = Resistor [tolerance=±5% resistance=470 package=THT]
  R8 = Resistor [tolerance=±5% resistance=470 package=THT]
  Mosfet_Connection = screw terminal, 3 pins
  D_Button = Pushbutton [package="[THT]"]
  C_Button = Pushbutton [package="[THT]"]
  KEYBOARD = Generic male header - 8 pins [package=THT]
  Part1 = Arduino Mega 2560 (Rev3)
  NEOPIXEL1 = Neopixel Strip -- White (60/m)
  NEOPIXEL2 = Neopixel Strip -- White (60/m)
  LCD2 = 16x2 I2C LCD screen
  Tiny_RTC1 = Tiny RTC
  microSD1 = MicroSD Breakout
  Mosfet_Connection1 = screw terminal, 4 pins
  C5 = Electrolytic Capacitor 470 uf [package="0807 [SMD, electrolytic]"]
  C6 = Electrolytic Capacitor 470 uf [package="0807 [SMD, electrolytic]"]
  Power_plug1 = Power plug
  LM2940CT-1 = Voltage Regulator - 5V
  C7 = Capacitor [package=cap-pth-5mm]  # not connected
  C8 = Capacitor [package=cap-pth-small-kit]  # not connected
  C9 = Capacitor [package=cap-pth-small-kit]
  C10 = Capacitor [package=cap-pth-small-kit]
  C11 = Electrolytic Capacitor 470 uf [package="0807 [SMD, electrolytic]"]
  LM2940CT-2 = Voltage Regulator - 5V
  C12 = Electrolytic Capacitor 470 uf [package="0807 [SMD, electrolytic]"]
  LM2940CT-3 = Voltage Regulator - 5V
  C13 = Electrolytic Capacitor 470 uf [package="0807 [SMD, electrolytic]"]
  C14 = Electrolytic Capacitor 470 uf [package="0807 [SMD, electrolytic]"]
  C15 = Capacitor [package=cap-pth-small-kit]
  C16 = Capacitor [package=cap-pth-small-kit]

nets:
  N1: SPKR1.pin1, Part1.D8_PWM
  GND: SPKR1.pin2, Mosfet_Connection.pin1, Part1.GND, NEOPIXEL1.GND, NEOPIXEL2.GND, LCD2.Ground, Tiny_RTC1.GND, microSD1.GND, Mosfet_Connection1.pin4, C5.-, C6.-, Power_plug1.GND, LM2940CT-1.GND, C9.2, C10.2, C11.-, LM2940CT-2.GND, C12.-, LM2940CT-3.GND, C13.-, C14.-, C15.2, C16.2
  N2: R7.Pin_0, Part1.D11_PWM
  N3: R7.Pin_1, NEOPIXEL2.+5V
  N4: R8.Pin_0, Part1.D10_PWM
  N5: R8.Pin_1, NEOPIXEL1.+5V
  5V: Mosfet_Connection.pin2, Part1.5V, LCD2.VCC, Tiny_RTC1.VCC, microSD1.5V, Mosfet_Connection1.pin1, C6.+, LM2940CT-1.output_voltage, C9.1, C11.+, LM2940CT-2.input_voltage, LM2940CT-3.input_voltage, C13.+, C15.1
  N6: Mosfet_Connection.pin3, Part1.D9_PWM
  N7: D_Button.Pin_1, D_Button.Pin_2, KEYBOARD.pin7, Part1.D13_PWM
  N8: D_Button.Pin_3, D_Button.Pin_4, C_Button.Pin_3, C_Button.Pin_4, KEYBOARD.pin4, Part1.A3
  N9: C_Button.Pin_2, KEYBOARD.pin8, Part1.D12_PWM
  N10: KEYBOARD.pin1, Part1.A0
  N11: KEYBOARD.pin2, Part1.A1
  N12: KEYBOARD.pin3, Part1.A2
  N13: KEYBOARD.pin5, Part1.A4
  N14: KEYBOARD.pin6, Part1.A5
  N15: Part1.D21/SCL, LCD2.SCL, Tiny_RTC1.SCL
  N16: Part1.D20/SDA, LCD2.SDA, Tiny_RTC1.SDA
  N17: Part1.D19/RX1, Mosfet_Connection1.pin3
  N18: Part1.D18/TX1, Mosfet_Connection1.pin2
  N19: Part1.D50, microSD1.DO
  N20: Part1.D51, microSD1.DI
  N21: Part1.D52, microSD1.CLK
  N22: Part1.D53, microSD1.CS
  N23: NEOPIXEL1.DI, C10.1, LM2940CT-2.output_voltage, C12.+
  N24: NEOPIXEL2.DI, LM2940CT-3.output_voltage, C14.+, C16.1
  N25: C5.+, Power_plug1.VCC, LM2940CT-1.input_voltage

notes:
  keyboard matrix 4x4
  'C' or Left button Connected to pin 4 & 7
  'D' or Right button
  Conected to pin 4 & 8
  Plan to use sainsmart lcd2004 20x4 LCD
  6v Rechargeable sealed lead battery
  36ah or more
  Needed for 24-30 hour run time needed.
  Future Neo Ublox 7M
  Integration Plug
  Power Regulators to take the 6v battery and output 5v.
  Left to Right
  470uf 16v
  0.1uf
  LM2940CT-05
  0.1uf
  470uf 16v
  Need to verify that this regulation is correct and will work.
  I have 3 because they should give about 0.5-1amp which is good for board and sensors and then one setup per MS2812 LED runs. Will add head shield to the regulators to reduce heat.

custom parts:
  Neopixel Strip -- White (60/m): Neopixel Strip, White, 60 pixels per meter.
  16x2 I2C LCD screen: Simple edit to LCD to represent the I2C LCD's on the market. A standard character display, usually with 2x16 characters. Comes in many colors.
  Tiny RTC: Tiny RTC I2C module DS1370Z RTC and AT24C32 EEPROM
  MicroSD Breakout: 5V-ready microSD Breakout with Level Shifter
  Electrolytic Capacitor 470 uf: A smd electrolytic capacitor.
  Voltage Regulator - 5V: 5V DC Voltage Regulator
